// Logisim project proj.circ as structural Verilog: 11 circuits, main circuit game
module game (
);

  wire button_1_out, button_2_out, button_3_out;
  wire [3:0] main_1_maxs0, main_1_maxs1, main_1_maxs2, main_1_maxs3, main_1_score0, main_1_score1,
       main_1_score2, main_1_score3;
  wire [23:0] main_1_out_4, main_1_out_9, main_1_out_10, main_1_out_11, main_1_out_12, main_1_out_13,
       main_1_out_14, main_1_out_19, main_1_out_20, main_1_out_21, main_1_out_22, main_1_out_23,
       main_1_out_24, main_1_out_25, main_1_out_26, main_1_out_27, main_1_out_28, main_1_out_29,
       main_1_out_30, main_1_out_31, main_1_out_32, main_1_out_33, main_1_out_34, main_1_out_35,
       main_1_out_36, main_1_out_37, main_1_out_38, main_1_out_39, main_1_out_40, main_1_out_41,
       main_1_out_42, main_1_out_43;

  DotMatrix #(.inputtype("row"), .matrixcols(24), .matrixrows(32)) dotmatrix_1 (
    .row0(main_1_out_4), .row1(main_1_out_9), .row2(main_1_out_10), .row3(main_1_out_11),
    .row4(main_1_out_12), .row5(main_1_out_13), .row6(main_1_out_14), .row7(main_1_out_19),
    .row8(main_1_out_20), .row9(main_1_out_21), .row10(main_1_out_22), .row11(main_1_out_23),
    .row12(main_1_out_24), .row13(main_1_out_25), .row14(main_1_out_26), .row15(main_1_out_27),
    .row16(main_1_out_28), .row17(main_1_out_29), .row18(main_1_out_30), .row19(main_1_out_31),
    .row20(main_1_out_32), .row21(main_1_out_33), .row22(main_1_out_34), .row23(main_1_out_35),
    .row24(main_1_out_36), .row25(main_1_out_37), .row26(main_1_out_38), .row27(main_1_out_39),
    .row28(main_1_out_40), .row29(main_1_out_41), .row30(main_1_out_42), .row31(main_1_out_43));
  main main_1 (
    .out_4(main_1_out_4), .out_9(main_1_out_9), .out_10(main_1_out_10), .out_11(main_1_out_11),
    .out_12(main_1_out_12), .out_13(main_1_out_13), .out_14(main_1_out_14), .out_19(main_1_out_19),
    .out_20(main_1_out_20), .out_21(main_1_out_21), .out_22(main_1_out_22), .out_23(main_1_out_23),
    .out_24(main_1_out_24), .out_25(main_1_out_25), .out_26(main_1_out_26), .out_27(main_1_out_27),
    .out_28(main_1_out_28), .out_29(main_1_out_29), .out_30(main_1_out_30), .out_31(main_1_out_31),
    .out_32(main_1_out_32), .out_33(main_1_out_33), .out_34(main_1_out_34), .out_35(main_1_out_35),
    .out_36(main_1_out_36), .out_37(main_1_out_37), .out_38(main_1_out_38), .out_39(main_1_out_39),
    .out_40(main_1_out_40), .out_41(main_1_out_41), .out_42(main_1_out_42), .out_43(main_1_out_43),
    .score2(main_1_score2), .score1(main_1_score1), .score0(main_1_score0), .in_2(button_2_out),
    .in_3(button_3_out), .loadStartField(button_1_out), .score3(main_1_score3), .maxS3(main_1_maxs3),
    .maxS1(main_1_maxs1), .maxS2(main_1_maxs2), .maxS0(main_1_maxs0));
  Hex_Digit_Display hex_digit_display_1 (.value(main_1_score3));  // open: dp
  Hex_Digit_Display hex_digit_display_2 (.value(main_1_score2));  // open: dp
  Button button_1 (.out(button_1_out));
  Hex_Digit_Display hex_digit_display_3 (.value(main_1_score1));  // open: dp
  Hex_Digit_Display hex_digit_display_4 (.value(main_1_score0));  // open: dp
  Button button_2 (.out(button_2_out));
  Button button_3 (.out(button_3_out));
  Hex_Digit_Display hex_digit_display_5 (.value(main_1_maxs2));  // open: dp
  Hex_Digit_Display hex_digit_display_6 (.value(main_1_maxs3));  // open: dp
  Hex_Digit_Display hex_digit_display_7 (.value(main_1_maxs0));  // open: dp
  Hex_Digit_Display hex_digit_display_8 (.value(main_1_maxs1));  // open: dp
endmodule

module main (
  input  loadStartField,
  input  in_2,
  input  in_3,
  output [23:0] out_4,
  output [3:0] score3,
  output [3:0] score2,
  output [3:0] score1,
  output [3:0] score0,
  output [23:0] out_9,
  output [23:0] out_10,
  output [23:0] out_11,
  output [23:0] out_12,
  output [23:0] out_13,
  output [23:0] out_14,
  output [3:0] maxS3,
  output [3:0] maxS2,
  output [3:0] maxS1,
  output [3:0] maxS0,
  output [23:0] out_19,
  output [23:0] out_20,
  output [23:0] out_21,
  output [23:0] out_22,
  output [23:0] out_23,
  output [23:0] out_24,
  output [23:0] out_25,
  output [23:0] out_26,
  output [23:0] out_27,
  output [23:0] out_28,
  output [23:0] out_29,
  output [23:0] out_30,
  output [23:0] out_31,
  output [23:0] out_32,
  output [23:0] out_33,
  output [23:0] out_34,
  output [23:0] out_35,
  output [23:0] out_36,
  output [23:0] out_37,
  output [23:0] out_38,
  output [23:0] out_39,
  output [23:0] out_40,
  output [23:0] out_41,
  output [23:0] out_42,
  output [23:0] out_43
);

  wire and_1_out, clock, clock_1_out, clock_2_out, collision, controlled_buffer_1_out,
       controlled_buffer_2_out, controlled_buffer_12_out, controlled_buffer_13_out, controlled_buffer_14_out,
       counter_6_carry, counter_7_carry, counter_10_carry, down, \end , fst, Jump, load, not_1_out,
       not_2_out, not_3_out, or_1_out, or_2_out, or_3_out, or_4_out, snd, up;
  wire [1:0] counter_4_q;
  wire [3:0] undriven;
  wire [4:0] colPos1, colPos2, counter_8_q, counter_9_q, getrandom_1_bus_0, rowPos;
  wire [7:0] r1, r2;
  wire [23:0] char, intro0, intro1, intro2, intro3, intro4, intro5, intro6, intro7, intro8,
       introstart_1_out_1, introstart_1_out_2, introstart_1_out_3, introstart_1_out_4, introstart_1_out_5,
       introstart_1_out_6, introstart_1_out_7, introstart_1_out_8, introstart_1_out_9, multiplexer_1_out,
       row0, row1, row2, row3, row4, row5, row6, row7, row8, row9, row10, row11, row12, row13, row14, row15,
       row16, row17, row18, row19, row20, row21, row22, row23, row24, row25, row26, row27, row28, row29,
       row30, row31, shifter_1_out, shifter_2_out, startgamefield_1_out_1, startgamefield_1_out_2,
       startgamefield_1_out_3, startgamefield_1_out_4, startgamefield_1_out_5, startgamefield_1_out_6,
       startgamefield_1_out_7, startgamefield_1_out_8, startgamefield_1_out_9, startgamefield_1_out_10,
       startgamefield_1_out_11, startgamefield_1_out_12, startgamefield_1_out_13, startgamefield_1_out_14,
       startgamefield_1_out_15, startgamefield_1_out_16, startgamefield_1_out_17, startgamefield_1_out_18,
       startgamefield_1_out_19, startgamefield_1_out_20, startgamefield_1_out_21, startgamefield_1_out_22,
       startgamefield_1_out_23, startgamefield_1_out_24, startgamefield_1_out_25, startgamefield_1_out_26,
       startgamefield_1_out_27, startgamefield_1_out_28, startgamefield_1_out_29, startgamefield_1_out_30,
       startgamefield_1_out_31, startgamefield_1_out_32, str0, str1, str2, str3, str4, str5, str6, str7,
       str8, str9, str10, str11, str12, str13, str14, str15, str16, str17, str18, str19, str20, str21, str22,
       str23, str24, str25, str26, str27, str28, str29, str30, str31;

  Clock clock_1 (.out(clock_1_out));
  not not_1 (not_1_out, load);
  assign controlled_buffer_1_out = load ? clock : 1'bz;  // Controlled_Buffer controlled_buffer_1
  Pull_Resistor pull_resistor_1 (.node(controlled_buffer_1_out));
  or or_1 (or_1_out, loadStartField, \end );
  getRandom getrandom_1 (.clock(clock_1_out), .bus_0(getrandom_1_bus_0));
  assign controlled_buffer_2_out = fst ? clock : 1'bz;  // Controlled_Buffer controlled_buffer_2
  movement movement_1 (.movement(r2), .collision(Jump), .clock(clock), .isMoving(fst));
  Counter #(.width(5), .max('h17)) counter_1 (
    .load(load), .D(5'b01011), .count(not_1_out), .Q(colPos1), .clk(or_2_out));  // open: carry, clr
  or or_2 (or_2_out, controlled_buffer_1_out, in_2);
  Counter #(.width(5), .max('h17)) counter_2 (.Q(colPos2), .clk(in_3), .clr(load));  // open: load, D, count, carry
  Counter #(.width(1), .max('h1)) counter_3 (.carry(load), .clk(or_1_out));  // open: load, D, count, Q, clr
  Shifter #(.width(24)) shifter_1 (.in({{20{1'b0}}, undriven}), .\dist (getrandom_1_bus_0), .out(shifter_1_out));
  Counter #(.width(2), .max('h3)) counter_4 (
    .Q(counter_4_q), .clk(controlled_buffer_2_out));  // open: load, D, count, carry, clr
  Multiplexer #(.select(2), .width(24), .enable("false")) multiplexer_1 (
    .in0(shifter_1_out), .in1({24{1'b0}}), .in2(shifter_1_out), .in3({24{1'b0}}), .out(multiplexer_1_out),
    .sel(counter_4_q));
  Pull_Resistor pull_resistor_2 (.node(controlled_buffer_2_out));
  Shift_Register #(.width(24), .length(32)) shiftRegister (
    .shift(1'b1), .in(multiplexer_1_out), .clk(or_3_out), .load(load), .d0(startgamefield_1_out_32),
    .q0(str31), .d1(startgamefield_1_out_31), .q1(str30), .d2(startgamefield_1_out_30), .q2(str29),
    .d3(startgamefield_1_out_29), .q3(str28), .d4(startgamefield_1_out_28), .q4(str27),
    .d5(startgamefield_1_out_27), .q5(str26), .d6(startgamefield_1_out_26), .q6(str25),
    .d7(startgamefield_1_out_25), .q7(str24), .d8(startgamefield_1_out_24), .q8(str23),
    .d9(startgamefield_1_out_23), .q9(str22), .d10(startgamefield_1_out_22), .q10(str21),
    .d11(startgamefield_1_out_21), .q11(str20), .d12(startgamefield_1_out_20), .q12(str19),
    .d13(startgamefield_1_out_19), .q13(str18), .d14(startgamefield_1_out_18), .q14(str17),
    .d15(startgamefield_1_out_17), .q15(str16), .d16(startgamefield_1_out_16), .q16(str15),
    .d17(startgamefield_1_out_15), .q17(str14), .d18(startgamefield_1_out_14), .q18(str13),
    .d19(startgamefield_1_out_13), .q19(str12), .d20(startgamefield_1_out_12), .q20(str11),
    .d21(startgamefield_1_out_11), .q21(str10), .d22(startgamefield_1_out_10), .q22(str9),
    .d23(startgamefield_1_out_9), .q23(str8), .d24(startgamefield_1_out_8), .q24(str7),
    .d25(startgamefield_1_out_7), .q25(str6), .d26(startgamefield_1_out_6), .q26(str5),
    .d27(startgamefield_1_out_5), .q27(str4), .d28(startgamefield_1_out_4), .q28(str3),
    .d29(startgamefield_1_out_3), .q29(str2), .d30(startgamefield_1_out_2), .q30(str1),
    .d31(startgamefield_1_out_1), .q31(str0));  // open: out, clr
  or or_3 (or_3_out, load, controlled_buffer_2_out);
  doodler doodler_1 (
    .colPos1(colPos1), .colPos2(colPos2), .rowPos(rowPos), .left(in_2), .right(in_3), .jump(snd),
    .out_7(row31), .out_8(row30), .out_9(row29), .out_10(row28), .out_11(row27), .out_12(row26),
    .out_13(row25), .out_14(row24), .out_15(row23), .out_16(row22), .out_17(row21), .out_18(row20),
    .out_19(row19), .out_20(row18), .out_21(row17), .out_22(row16), .out_23(row15), .out_24(row14),
    .out_25(row13), .out_26(row12), .out_27(row11), .out_28(row10), .out_29(row9), .out_30(row8),
    .out_31(row7), .out_32(row6), .out_33(row5), .out_34(row4), .out_35(row3), .out_36(row2), .out_37(row1),
    .out_38(row0));
  Shifter #(.width(24), .shift("rl")) shifter_2 (.in(24'h5), .\dist (colPos1), .out(shifter_2_out));
  Shifter #(.width(24), .shift("rr")) shifter_3 (.in(shifter_2_out), .\dist (colPos2), .out(char));
  introStart introstart_1 (
    .out_1(introstart_1_out_1), .out_2(introstart_1_out_2), .out_3(introstart_1_out_3),
    .out_4(introstart_1_out_4), .out_5(introstart_1_out_5), .out_6(introstart_1_out_6),
    .out_7(introstart_1_out_7), .out_8(introstart_1_out_8), .out_9(introstart_1_out_9));
  startGameField startgamefield_1 (
    .out_1(startgamefield_1_out_1), .out_2(startgamefield_1_out_2), .out_3(startgamefield_1_out_3),
    .out_4(startgamefield_1_out_4), .out_5(startgamefield_1_out_5), .out_6(startgamefield_1_out_6),
    .out_7(startgamefield_1_out_7), .out_8(startgamefield_1_out_8), .out_9(startgamefield_1_out_9),
    .out_10(startgamefield_1_out_10), .out_11(startgamefield_1_out_11), .out_12(startgamefield_1_out_12),
    .out_13(startgamefield_1_out_13), .out_14(startgamefield_1_out_14), .out_15(startgamefield_1_out_15),
    .out_16(startgamefield_1_out_16), .out_17(startgamefield_1_out_17), .out_18(startgamefield_1_out_18),
    .out_19(startgamefield_1_out_19), .out_20(startgamefield_1_out_20), .out_21(startgamefield_1_out_21),
    .out_22(startgamefield_1_out_22), .out_23(startgamefield_1_out_23), .out_24(startgamefield_1_out_24),
    .out_25(startgamefield_1_out_25), .out_26(startgamefield_1_out_26), .out_27(startgamefield_1_out_27),
    .out_28(startgamefield_1_out_28), .out_29(startgamefield_1_out_29), .out_30(startgamefield_1_out_30),
    .out_31(startgamefield_1_out_31), .out_32(startgamefield_1_out_32));
  not not_2 (not_2_out, fst);
  Counter #(.width(4), .max('h9), .trigger("falling")) counter_5 (
    .Q(score3), .clk(counter_6_carry), .clr(loadStartField));  // open: load, D, count, carry
  checkCollision checkcollision_1 (
    .str0(str31), .str1(str30), .str2(str29), .str3(str28), .str4(str27), .str5(str26), .str6(str25),
    .str7(str24), .str8(str23), .str9(str22), .str10(str21), .str11(str20), .str12(str19), .str13(str18),
    .str14(str17), .str15(str16), .str16(str15), .str17(str14), .str18(str13), .str19(str12), .str20(str11),
    .str21(str10), .str22(str9), .str23(str8), .str24(str7), .str25(str6), .str26(str5), .str27(str4),
    .str28(str3), .str29(str2), .str30(str1), .str31(str0), .rowPos(rowPos), .char(char), .out(collision));
  assign intro0 = load ? introstart_1_out_1 : 24'bz;  // Controlled_Buffer controlled_buffer_3
  Pull_Resistor pull_resistor_3 (.node(intro0));
  Pull_Resistor pull_resistor_4 (.node(intro1));
  assign intro1 = load ? introstart_1_out_2 : 24'bz;  // Controlled_Buffer controlled_buffer_4
  assign intro2 = load ? introstart_1_out_3 : 24'bz;  // Controlled_Buffer controlled_buffer_5
  Pull_Resistor pull_resistor_5 (.node(intro2));
  Pull_Resistor pull_resistor_6 (.node(intro3));
  assign intro3 = load ? introstart_1_out_4 : 24'bz;  // Controlled_Buffer controlled_buffer_6
  assign intro4 = load ? introstart_1_out_5 : 24'bz;  // Controlled_Buffer controlled_buffer_7
  Pull_Resistor pull_resistor_7 (.node(intro4));
  assign intro5 = load ? introstart_1_out_6 : 24'bz;  // Controlled_Buffer controlled_buffer_8
  Pull_Resistor pull_resistor_8 (.node(intro5));
  assign intro6 = load ? introstart_1_out_7 : 24'bz;  // Controlled_Buffer controlled_buffer_9
  Pull_Resistor pull_resistor_9 (.node(intro6));
  assign intro7 = load ? introstart_1_out_8 : 24'bz;  // Controlled_Buffer controlled_buffer_10
  Pull_Resistor pull_resistor_10 (.node(intro7));
  assign intro8 = load ? introstart_1_out_9 : 24'bz;  // Controlled_Buffer controlled_buffer_11
  Pull_Resistor pull_resistor_11 (.node(intro8));
  and and_1 (and_1_out, not_2_out, snd);
  Counter #(.width(4), .max('h9), .trigger("falling")) counter_6 (
    .Q(score2), .carry(counter_6_carry), .clk(counter_7_carry), .clr(loadStartField));  // open: load, D, count
  movement movement_2 (.movement(r1), .collision(and_1_out), .clock(clock), .isMoving(up));
  or or_4 (or_4_out, up, load);
  assign controlled_buffer_12_out = or_4_out ? clock : 1'bz;  // Controlled_Buffer controlled_buffer_12
  assign controlled_buffer_13_out = down ? clock : 1'bz;  // Controlled_Buffer controlled_buffer_13
  processor processor_1 (
    .jumpInter(Jump), .rowPos(rowPos), .val1({score3, score2}), .val0({score1, score0}),
    .maxScoreInter(load), .maxScore0({maxS3, maxS2}), .maxScore1({maxS1, maxS0}), .stage0(r2), .stage1(r1));
  Counter #(.width(4), .max('h9), .trigger("falling")) counter_7 (
    .Q(score1), .carry(counter_7_carry), .clk(counter_10_carry), .clr(loadStartField));  // open: load, D, count
  assign controlled_buffer_14_out = fst ? clock : 1'bz;  // Controlled_Buffer controlled_buffer_14
  not not_3 (not_3_out, load);
  Counter #(.width(5), .max('h1f)) counter_8 (
    .load(load), .D(5'b00101), .count(not_3_out), .Q(counter_8_q), .clk(controlled_buffer_12_out));  // open: carry, clr
  Pull_Resistor pull_resistor_12 (.node(controlled_buffer_12_out));
  Counter #(.width(5), .max('h1f), .trigger("falling")) counter_9 (
    .Q(counter_9_q), .clk(controlled_buffer_13_out), .clr(load));  // open: load, D, count, carry
  Pull_Resistor pull_resistor_13 (.node(controlled_buffer_13_out));
  Counter #(.width(4), .max('h9), .trigger("falling")) counter_10 (
    .Q(score0), .carry(counter_10_carry), .clk(controlled_buffer_14_out), .clr(loadStartField));  // open: load, D, count
  Pull_Resistor pull_resistor_14 (.node(controlled_buffer_14_out));
  Subtractor #(.width(5)) subtractor_1 (.a(counter_8_q), .b(counter_9_q), .out(rowPos));  // open: bin, bout
  Comparator #(.width(5)) comparator_1 (.a(rowPos), .b({5{1'b1}}), .eq(\end ));  // open: gt, lt
  movement movement_3 (.movement(8'h7), .collision(Jump), .clock(clock), .isMoving(snd));
  assign out_4 = str31 | row31;  // OR_Gate or_5, 24 bits wide
  assign out_9 = str30 | row30;  // OR_Gate or_6, 24 bits wide
  assign out_10 = str29 | intro0 | row29;  // OR_Gate or_7, 24 bits wide
  assign out_11 = str28 | intro1 | row28;  // OR_Gate or_8, 24 bits wide
  assign out_12 = str27 | intro2 | row27;  // OR_Gate or_9, 24 bits wide
  assign out_13 = str26 | intro3 | row26;  // OR_Gate or_10, 24 bits wide
  assign out_14 = str25 | intro4 | row25;  // OR_Gate or_11, 24 bits wide
  assign out_19 = str24 | intro5 | row24;  // OR_Gate or_12, 24 bits wide
  assign out_20 = str23 | intro6 | row23;  // OR_Gate or_13, 24 bits wide
  assign out_21 = str22 | intro7 | row22;  // OR_Gate or_14, 24 bits wide
  assign out_22 = str21 | intro8 | row21;  // OR_Gate or_15, 24 bits wide
  assign out_23 = str20 | row20;  // OR_Gate or_16, 24 bits wide
  assign out_24 = str19 | row19;  // OR_Gate or_17, 24 bits wide
  assign out_25 = str18 | row18;  // OR_Gate or_18, 24 bits wide
  assign out_26 = str17 | row17;  // OR_Gate or_19, 24 bits wide
  assign out_27 = str16 | row16;  // OR_Gate or_20, 24 bits wide
  assign out_28 = str15 | row15;  // OR_Gate or_21, 24 bits wide
  assign out_29 = str14 | row14;  // OR_Gate or_22, 24 bits wide
  assign out_30 = str13 | row13;  // OR_Gate or_23, 24 bits wide
  assign out_31 = str12 | row12;  // OR_Gate or_24, 24 bits wide
  assign out_32 = str11 | row11;  // OR_Gate or_25, 24 bits wide
  assign out_33 = str10 | row10;  // OR_Gate or_26, 24 bits wide
  assign out_34 = str9 | row9;  // OR_Gate or_27, 24 bits wide
  assign out_35 = str8 | row8;  // OR_Gate or_28, 24 bits wide
  assign out_36 = str7 | row7;  // OR_Gate or_29, 24 bits wide
  assign out_37 = str6 | row6;  // OR_Gate or_30, 24 bits wide
  assign out_38 = str5 | row5;  // OR_Gate or_31, 24 bits wide
  assign out_39 = str4 | row4;  // OR_Gate or_32, 24 bits wide
  assign out_40 = str3 | row3;  // OR_Gate or_33, 24 bits wide
  assign out_41 = str2 | row2;  // OR_Gate or_34, 24 bits wide
  assign out_42 = str1 | row1;  // OR_Gate or_35, 24 bits wide
  assign out_43 = str0 | row0;  // OR_Gate or_36, 24 bits wide
  Clock clock_2 (.out(clock_2_out));
  nor nor_1 (down, snd, fst, collision, up);
  Counter #(.width(6), .max('h3f)) counter_11 (.carry(clock), .clk(clock_2_out));  // open: load, D, count, Q, clr
  and and_2 (Jump, ~down, ~snd, collision);  // AND_Gate

  // Other names for the same wires on the sheet: left = in_2; max0[7:0] = {maxS1, maxS0}; max1[7:0] = {maxS3, maxS2};
  //   reset = loadStartField; right = in_3; val0[7:0] = {score1, score0}; val1[7:0] = {score3, score2}

  // Notes on the sheet:
  //   out_9: pull=up
  //   out_32: pull=up
  //   out_27: pull=up
  //   out_13: pull=up
  //   out_31: pull=up
  //   out_19: pull=up
  //   out_33: pull=up
  //   out_36: pull=up
  //   out_38: pull=up
  //   out_25: pull=up
  //   out_30: pull=up
  //   out_37: pull=up
  //   out_41: pull=up
  //   out_39: pull=up
  //   out_4: pull=up
  //   out_43: pull=up
  //   out_40: pull=up
  //   out_22: pull=up
  //   out_12: pull=up
  //   out_10: pull=up
  //   out_23: pull=up
  //   out_29: pull=up
  //   out_24: pull=up
  //   out_42: pull=up
  //   out_28: pull=up
  //   out_35: pull=up
  //   out_14: pull=up
  //   out_34: pull=up
  //   out_20: pull=up
  //   out_11: pull=up
  //   out_21: pull=up
  //   out_26: pull=up
  //   firstStageOfjump
  //   charSprite
  //   charPosition
  //   loadStartField
  //   checkCollision
  //   loadStartPic
  //   scoreOutput
  //   maxScoreOutput
  //   secondStageOfJump
  //   calc JumpStages and MaxScore
  //   checkDeath
  //   fullJumpStage
  //   outputField
  //   checkFall
  //   checkJump
  //   clock
endmodule

module checkCollision (
  input  [4:0] rowPos,
  input  [23:0] char,
  input  [23:0] str0,
  input  [23:0] str1,
  input  [23:0] str2,
  input  [23:0] str3,
  input  [23:0] str4,
  input  [23:0] str5,
  input  [23:0] str6,
  input  [23:0] str7,
  input  [23:0] str8,
  input  [23:0] str9,
  input  [23:0] str10,
  input  [23:0] str11,
  input  [23:0] str12,
  input  [23:0] str13,
  input  [23:0] str14,
  input  [23:0] str15,
  input  [23:0] str16,
  input  [23:0] str17,
  input  [23:0] str18,
  input  [23:0] str19,
  input  [23:0] str20,
  input  [23:0] str21,
  input  [23:0] str22,
  input  [23:0] str23,
  input  [23:0] str24,
  input  [23:0] str25,
  input  [23:0] str26,
  input  [23:0] str27,
  input  [23:0] str28,
  input  [23:0] str29,
  input  [23:0] str30,
  input  [23:0] str31,
  output out
);

  wire [23:0] and_1_out, multiplexer_1_out;

  Multiplexer #(.select(5), .width(24), .disabled(0), .enable("false")) multiplexer_1 (
    .in0({24{1'b0}}), .in1(str31), .in2(str30), .in3(str29), .in4(str28), .in5(str27), .in6(str26),
    .in7(str25), .in8(str24), .in9(str23), .in10(str22), .in11(str21), .in12(str20), .in13(str19),
    .in14(str18), .in15(str17), .in16(str16), .in17(str15), .in18(str14), .in19(str13), .in20(str12),
    .in21(str11), .in22(str10), .in23(str9), .in24(str8), .in25(str7), .in26(str6), .in27(str5), .in28(str4),
    .in29(str3), .in30(str2), .in31(str1), .out(multiplexer_1_out), .sel(rowPos));
  // Probe on multiplexer_1_out
  // Probe on char
  assign and_1_out = multiplexer_1_out & char;  // AND_Gate and_1, 24 bits wide
  or or_1 (out, and_1_out[0], and_1_out[1], and_1_out[2], and_1_out[3], and_1_out[4], and_1_out[5], and_1_out[6], and_1_out[7], and_1_out[8], and_1_out[9], and_1_out[10], and_1_out[11], and_1_out[12], and_1_out[13], and_1_out[14], and_1_out[15], and_1_out[16], and_1_out[17], and_1_out[18], and_1_out[19], and_1_out[20], and_1_out[21], and_1_out[22], and_1_out[23]);

  // Other names for the same wires on the sheet: str0_t[23:0] = str31; str1_t[23:0] = str30; str2_t[23:0] = str29;
  //   str3_t[23:0] = str28; str4_t[23:0] = str27; str5_t[23:0] = str26; str6_t[23:0] = str25; str7_t[23:0] = str24;
  //   str8_t[23:0] = str23; str9_t[23:0] = str22; str10_t[23:0] = str21; str11_t[23:0] = str20; str12_t[23:0] = str19;
  //   str13_t[23:0] = str18; str14_t[23:0] = str17; str15_t[23:0] = str16; str16_t[23:0] = str15;
  //   str17_t[23:0] = str14; str18_t[23:0] = str13; str19_t[23:0] = str12; str20_t[23:0] = str11;
  //   str21_t[23:0] = str10; str22_t[23:0] = str9; str23_t[23:0] = str8; str24_t[23:0] = str7; str25_t[23:0] = str6;
  //   str26_t[23:0] = str5; str27_t[23:0] = str4; str28_t[23:0] = str3; str29_t[23:0] = str2; str30_t[23:0] = str1;
  //   str31_t[23:0] = str0

  // Notes on the sheet:
  //   str29: pull=up
  //   str2: pull=up
  //   str16: pull=up
  //   str18: pull=up
  //   str15: pull=up
  //   str4: pull=up
  //   str24: pull=up
  //   str6: pull=up
  //   str27: pull=up
  //   str21: pull=up
  //   str11: pull=up
  //   str8: pull=up
  //   char: pull=up
  //   str5: pull=up
  //   str26: pull=up
  //   str22: pull=up
  //   str12: pull=up
  //   str1: pull=up
  //   str30: pull=up
  //   str23: pull=up
  //   str3: pull=up
  //   str10: pull=up
  //   str9: pull=up
  //   str28: pull=up
  //   str17: pull=up
  //   str7: pull=up
  //   str31: pull=up
  //   str20: pull=up
  //   str25: pull=up
  //   str14: pull=up
  //   str13: pull=up
  //   str0: pull=up
  //   str19: pull=up
endmodule

// OR
module _5BitOr (
  input  [4:0] num,
  output out
);

  or or_1 (out, num[0], num[1], num[2], num[3], num[4]);
endmodule

module startGameField (
  output [23:0] out_1,
  output [23:0] out_2,
  output [23:0] out_3,
  output [23:0] out_4,
  output [23:0] out_5,
  output [23:0] out_6,
  output [23:0] out_7,
  output [23:0] out_8,
  output [23:0] out_9,
  output [23:0] out_10,
  output [23:0] out_11,
  output [23:0] out_12,
  output [23:0] out_13,
  output [23:0] out_14,
  output [23:0] out_15,
  output [23:0] out_16,
  output [23:0] out_17,
  output [23:0] out_18,
  output [23:0] out_19,
  output [23:0] out_20,
  output [23:0] out_21,
  output [23:0] out_22,
  output [23:0] out_23,
  output [23:0] out_24,
  output [23:0] out_25,
  output [23:0] out_26,
  output [23:0] out_27,
  output [23:0] out_28,
  output [23:0] out_29,
  output [23:0] out_30,
  output [23:0] out_31,
  output [23:0] out_32
);

  wire [3:0] def;

  Shifter #(.width(24)) shifter_1 (.in({{20{1'b0}}, def}), .\dist (5'b01010), .out(out_3));
  Shifter #(.width(24)) shifter_2 (.in({{20{1'b0}}, def}), .\dist (5'b00101), .out(out_5));
  Shifter #(.width(24)) shifter_3 (.in({{20{1'b0}}, def}), .\dist (5'b10100), .out(out_7));
  Shifter #(.width(24)) shifter_4 (.in({{20{1'b0}}, def}), .\dist (5'b00100), .out(out_9));
  Shifter #(.width(24)) shifter_5 (.in({{20{1'b0}}, def}), .\dist (5'b10001), .out(out_11));
  Shifter #(.width(24)) shifter_6 (.in({{20{1'b0}}, def}), .\dist (5'b01100), .out(out_13));
  Shifter #(.width(24)) shifter_7 (.in({{20{1'b0}}, def}), .\dist (5'b10010), .out(out_15));
  Shifter #(.width(24)) shifter_8 (.in({{20{1'b0}}, def}), .\dist (5'b00101), .out(out_17));
  Shifter #(.width(24)) shifter_9 (.in({{20{1'b0}}, def}), .\dist (5'b00111), .out(out_19));
  Shifter #(.width(24)) shifter_10 (.in({{20{1'b0}}, def}), .\dist (5'b01101), .out(out_21));
  Shifter #(.width(24)) shifter_11 (.in({{20{1'b0}}, def}), .\dist (5'b00111), .out(out_23));
  Shifter #(.width(24)) shifter_12 (.in({{20{1'b0}}, def}), .\dist (5'b10010), .out(out_25));
  Shifter #(.width(24)) shifter_13 (.in({{20{1'b0}}, def}), .\dist (5'b00010), .out(out_27));
  Shifter #(.width(24)) shifter_14 (.in({{20{1'b0}}, def}), .\dist (5'b01010), .out(out_29));
  Shifter #(.width(24)) shifter_15 (.in({{20{1'b0}}, def}), .\dist (5'b01101), .out(out_31));

  assign out_1 = {24{1'b0}};
  assign out_2 = {24{1'b0}};
  assign out_4 = {24{1'b0}};
  assign out_6 = {24{1'b0}};
  assign out_8 = {24{1'b0}};
  assign out_10 = {24{1'b0}};
  assign out_12 = {24{1'b0}};
  assign out_14 = {24{1'b0}};
  assign out_16 = {24{1'b0}};
  assign out_18 = {24{1'b0}};
  assign out_20 = {24{1'b0}};
  assign out_22 = {24{1'b0}};
  assign out_24 = {24{1'b0}};
  assign out_26 = {24{1'b0}};
  assign out_28 = {24{1'b0}};
  assign out_30 = {24{1'b0}};
  assign out_32 = {24{1'b0}};
endmodule

// CPU
module processor (
  input  jumpInter,
  input  maxScoreInter,
  input  [4:0] rowPos,
  input  [7:0] val1,
  input  [7:0] val0,
  output [7:0] stage0,
  output [7:0] stage1,
  output [7:0] maxScore0,
  output [7:0] maxScore1
);

  wire and_2_out, and_3_out, and_4_out, and_5_out, and_6_out, cdm_8_mark5_1_data_inst,
       cdm_8_mark5_1_mem_cycle, clk, comparator_1_eq, comparator_1_gt, counter_1_carry, decoder_1_out0,
       decoder_1_out1, demultiplexer_1_out0, demultiplexer_1_out1, demultiplexer_1_out2, IAck, IOsel, IRQ,
       max0, max1, not_1_out, not_2_out, not_3_out, or_1_out, or_2_out, READwrite, xor_1_out;
  wire [2:0] vec;
  wire [3:0] IOaddr;
  wire [7:0] bit_extender_1_out, cdm_8_mark5_1_data_out, cdm_8_mark5_1_pc, cdm_8_mark5_1_ps,
       cdm_8_mark5_1_r3, cdm_8_mark5_1_sp, controlled_buffer_2_out, controlled_buffer_3_out,
       controlled_buffer_4_out, IOdat, r0;
  wire [7:4] cdm_8_mark5_1_addr;

  Clock clock_1 (.out(clk));
  // Probe on stage0
  // Probe on cdm_8_mark5_1_r3
  // Probe on stage1
  // Probe on r0
  // Probe on cdm_8_mark5_1_pc
  and and_1 (IOsel, cdm_8_mark5_1_addr[4], cdm_8_mark5_1_addr[5], cdm_8_mark5_1_addr[6], cdm_8_mark5_1_addr[7], decoder_1_out1);
  // Probe on cdm_8_mark5_1_ps
  // Probe on cdm_8_mark5_1_sp
  CdM_8_mark5 cdm_8_mark5_1 (
    .clock(clk), .addr({cdm_8_mark5_1_addr, IOaddr}), .mem_read(READwrite),
    .mem_cycle(cdm_8_mark5_1_mem_cycle), .data_inst(cdm_8_mark5_1_data_inst),
    .data_out(cdm_8_mark5_1_data_out), .data_in(controlled_buffer_2_out), .r0(r0), .r1(stage1), .r2(stage0),
    .r3(cdm_8_mark5_1_r3), .PC(cdm_8_mark5_1_pc), .SP(cdm_8_mark5_1_sp), .PS(cdm_8_mark5_1_ps), .IAck(IAck),
    .IRQ(IRQ), .vec(vec));
  Decoder #(.disabled(0)) decoder_1 (
    .out0(decoder_1_out0), .out1(decoder_1_out1), .sel(cdm_8_mark5_1_data_inst), .en(cdm_8_mark5_1_mem_cycle));
  not not_1 (not_1_out, READwrite);
  assign IOdat = not_1_out ? cdm_8_mark5_1_data_out : 8'bz;  // Controlled_Buffer controlled_buffer_1
  assign controlled_buffer_2_out = READwrite ? IOdat : 8'bz;  // Controlled_Buffer controlled_buffer_2
  // Probe on {cdm_8_mark5_1_addr, IOaddr}
  and and_2 (and_2_out, decoder_1_out1, ~IOsel);  // AND_Gate
  not not_2 (not_2_out, clk);
  // Probe on IOdat
  RAM ram_1 (
    .addr({cdm_8_mark5_1_addr, IOaddr}), .data(IOdat), .sel(and_2_out), .clk(not_2_out), .ld(READwrite));  // open: clr
  ROM rom_1 (.addr({cdm_8_mark5_1_addr, IOaddr}), .data(IOdat), .sel(decoder_1_out0));
  and and_3 (and_3_out, max1, ~READwrite);  // AND_Gate
  assign controlled_buffer_3_out = and_3_out ? val1 : 8'bz;  // Controlled_Buffer controlled_buffer_3
  assign controlled_buffer_4_out = and_4_out ? val0 : 8'bz;  // Controlled_Buffer controlled_buffer_4
  and and_4 (and_4_out, max0, ~READwrite);  // AND_Gate
  assign IOdat = demultiplexer_1_out0 ? bit_extender_1_out : 8'bz;  // Controlled_Buffer controlled_buffer_5
  assign IOdat = demultiplexer_1_out1 ? val1 : 8'bz;  // Controlled_Buffer controlled_buffer_6
  assign bit_extender_1_out = {{3{1'b0}}, rowPos};  // Bit_Extender bit_extender_1
  assign IOdat = demultiplexer_1_out2 ? val0 : 8'bz;  // Controlled_Buffer controlled_buffer_7
  Register register_1 (.D(controlled_buffer_3_out), .Q(maxScore0), .clk(clk));  // open: en, clr
  Register register_2 (.D(controlled_buffer_4_out), .Q(maxScore1), .clk(clk));  // open: en, clr
  assign IOdat = and_5_out ? maxScore0 : 8'bz;  // Controlled_Buffer controlled_buffer_8
  and and_5 (and_5_out, max1, READwrite);
  assign IOdat = and_6_out ? maxScore1 : 8'bz;  // Controlled_Buffer controlled_buffer_9
  and and_6 (and_6_out, max0, READwrite);
  // Probe on vec
  Demultiplexer #(.select(4), .disabled(0), .enable("false")) demultiplexer_1 (
    .out0(demultiplexer_1_out0), .out1(demultiplexer_1_out1), .out2(demultiplexer_1_out2), .out3(max1),
    .out4(max0), .in(IOsel), .sel(IOaddr));  // open: out5, out6, out7, out8, out9, out10, out11, out12, out13, out14, out15
  assign vec = jumpInter ? 3'b101 : 3'bz;  // Controlled_Buffer controlled_buffer_10
  assign vec = maxScoreInter ? 3'b110 : 3'bz;  // Controlled_Buffer controlled_buffer_11
  or or_1 (or_1_out, jumpInter, maxScoreInter);
  assign IRQ = not_3_out ? or_1_out : 1'bz;  // Controlled_Buffer controlled_buffer_12
  not not_3 (not_3_out, counter_1_carry);
  Counter #(.width(1), .max('h1)) counter_1 (.carry(counter_1_carry), .clk(or_2_out));  // open: load, D, count, Q, clr
  or or_2 (or_2_out, xor_1_out, comparator_1_eq);
  xor xor_1 (xor_1_out, or_1_out, comparator_1_gt);
  Comparator comparator_1 (.a(8'ha), .b(r0), .gt(comparator_1_gt), .eq(comparator_1_eq));  // open: lt
  Pull_Resistor pull_resistor_1 (.node(IRQ));

  // Other names for the same wires on the sheet: maxScore0_t[7:0] = maxScore1; maxScore1_t[7:0] = maxScore0;
  //   wr = READwrite

  // Notes on the sheet:
  //   contents of rom_1 (hex, n*v repeats v):
  //   cd f0 c1 d1 a c1 d1 80 c1 d9 c5 d5 ee b d3 f0 bf d0 b 7c e4 1c d1 0 d2 7 ee 2d d d2 3 76 ec 28 d1 7
  //   d2 0 ee 2d 31 d2 7 36 86 d0 0 d9 d1 f1 b5 d2 f3 ba 76 ed 44 d2 f3 a9 d1 f2 b5 d2 f4 a9 ee 59 76 e1
  //   59 d3 f2 bf d2 f4 ba 7e ed 59 d2 f4 ab d1 f1 b5 d2 f3 a9 d0 b d0 0 d9 156*0 e b 30 b
endmodule

// moveChip
module movement (
  input  [7:0] movement,
  input  collision,
  input  clock,
  output isMoving
);

  wire and_1_out, comparator_1_gt, xor_1_out;
  wire [4:0] bit_extender_1_out, multiplexer_1_out, register_1_q, subtractor_1_out;

  Bit_Extender #(.out_width(5)) bit_extender_1 (.in(movement), .out(bit_extender_1_out));
  and and_1 (and_1_out, isMoving, collision);
  Multiplexer #(.width(5), .enable("false")) multiplexer_1 (
    .in0(subtractor_1_out), .in1(bit_extender_1_out), .out(multiplexer_1_out), .sel(xor_1_out));
  xor xor_1 (xor_1_out, and_1_out, collision);
  Register #(.width(5)) register_1 (.D(multiplexer_1_out), .Q(register_1_q), .clk(clock));  // open: en, clr
  _5BitOr u_5bitor_1 (.num(register_1_q), .out(isMoving));
  Subtractor #(.width(5)) subtractor_1 (
    .a(register_1_q), .b({5{1'b0}}), .out(subtractor_1_out), .bin(comparator_1_gt));  // open: bout
  Comparator #(.width(5)) comparator_1 (.a(register_1_q), .b({5{1'b0}}), .gt(comparator_1_gt));  // open: eq, lt
endmodule

// randNum
module getRandom (
  input  clock,
  output [4:0] bus_0
);

  wire comparator_1_lt;
  wire [4:0] random_1_out;

  Random #(.width(5)) random_1 (.clk(clock), .out(random_1_out));  // open: next, clr
  Comparator #(.width(5), .mode("unsigned")) comparator_1 (
    .a(random_1_out), .b(5'b10101), .lt(comparator_1_lt));  // open: gt, eq
  Register #(.width(5)) register_1 (.D(random_1_out), .Q(bus_0), .clk(comparator_1_lt));  // open: en, clr
endmodule

module keyboard (
);

  wire clock_1_out, left, right;
  wire [6:0] keyboard_1_data;

  Clock clock_1 (.out(clock_1_out));
  Keyboard keyboard_1 (.clk(clock_1_out), .clr(clock_1_out), .data(keyboard_1_data));  // open: re, avail
  Comparator #(.width(7)) comparator_1 (.a(7'b1100001), .b(keyboard_1_data), .eq(left));  // open: gt, lt
  Comparator #(.width(7)) comparator_2 (.a(keyboard_1_data), .b(7'b1100100), .eq(right));  // open: gt, lt
endmodule

module doodler (
  input  [4:0] colPos1,
  input  left,
  input  right,
  input  jump,
  input  [4:0] colPos2,
  input  [4:0] rowPos,
  output [23:0] out_7,
  output [23:0] out_8,
  output [23:0] out_9,
  output [23:0] out_10,
  output [23:0] out_11,
  output [23:0] out_12,
  output [23:0] out_13,
  output [23:0] out_14,
  output [23:0] out_15,
  output [23:0] out_16,
  output [23:0] out_17,
  output [23:0] out_18,
  output [23:0] out_19,
  output [23:0] out_20,
  output [23:0] out_21,
  output [23:0] out_22,
  output [23:0] out_23,
  output [23:0] out_24,
  output [23:0] out_25,
  output [23:0] out_26,
  output [23:0] out_27,
  output [23:0] out_28,
  output [23:0] out_29,
  output [23:0] out_30,
  output [23:0] out_31,
  output [23:0] out_32,
  output [23:0] out_33,
  output [23:0] out_34,
  output [23:0] out_35,
  output [23:0] out_36,
  output [23:0] out_37,
  output [23:0] out_38
);

  wire left_t, right_t;
  wire [23:0] multiplexer_1_out, multiplexer_2_out, multiplexer_3_out, row0_0, row0_1, row0_2, row0_3,
       row0_4, row0_5, row0_6, row0_7, row0_8, row0_9, row0_10, row0_11, row0_12, row0_13, row0_14, row0_15,
       row0_16, row0_17, row0_18, row0_19, row0_20, row0_21, row0_22, row0_23, row0_24, row0_25, row0_26,
       row0_27, row0_28, row0_29, row0_30, row0_31, row1_0, row1_1, row1_2, row1_3, row1_4, row1_5, row1_6,
       row1_7, row1_8, row1_9, row1_10, row1_11, row1_12, row1_13, row1_14, row1_15, row1_16, row1_17,
       row1_18, row1_19, row1_20, row1_21, row1_22, row1_23, row1_24, row1_25, row1_26, row1_27, row1_28,
       row1_29, row1_30, row1_31, row2_0, row2_1, row2_2, row2_3, row2_4, row2_5, row2_6, row2_7, row2_8,
       row2_9, row2_10, row2_11, row2_12, row2_13, row2_14, row2_15, row2_16, row2_17, row2_18, row2_19,
       row2_20, row2_21, row2_22, row2_23, row2_24, row2_25, row2_26, row2_27, row2_28, row2_29, row2_30,
       row2_31, row3_0, row3_1, row3_2, row3_3, row3_4, row3_5, row3_6, row3_7, row3_8, row3_9, row3_10,
       row3_11, row3_12, row3_13, row3_14, row3_15, row3_16, row3_17, row3_18, row3_19, row3_20, row3_21,
       row3_22, row3_23, row3_24, row3_25, row3_26, row3_27, row3_28, row3_29, row3_30, row3_31,
       shifter_1_out, shifter_2_out, shifter_3_out, shifter_4_out, shifter_5_out, shifter_6_out,
       shifter_7_out, shifter_8_out;

  Multiplexer #(.width(24), .disabled(0), .enable("false")) multiplexer_1 (
    .in0(24'h800002), .in1(24'ha), .out(multiplexer_1_out), .sel(right_t));
  Multiplexer #(.width(24), .disabled(0), .enable("false")) multiplexer_2 (
    .in0(24'h5), .in1(multiplexer_1_out), .out(multiplexer_2_out), .sel(jump));
  Multiplexer #(.width(24), .disabled(0), .enable("false")) multiplexer_3 (
    .in0(24'hb), .in1(24'h800006), .out(multiplexer_3_out), .sel(right_t));
  Shifter #(.width(24), .shift("rl")) shifter_1 (.in(multiplexer_3_out), .\dist (colPos1), .out(shifter_1_out));
  Shifter #(.width(24), .shift("rl")) shifter_2 (.in(multiplexer_2_out), .\dist (colPos1), .out(shifter_2_out));
  Shifter #(.width(24), .shift("rr")) shifter_3 (.in(shifter_1_out), .\dist (colPos2), .out(shifter_3_out));
  Counter #(.width(1), .max('h1), .ongoal("load")) counter_1 (
    .D(1'b1), .carry(left_t), .clk(left), .clr(right));  // open: load, count, Q
  Shifter #(.width(24), .shift("rr")) shifter_4 (.in(shifter_2_out), .\dist (colPos2), .out(shifter_4_out));
  Demultiplexer #(.select(5), .width(24), .disabled(0), .enable("false")) demultiplexer_1 (
    .out0(row0_0), .out1(row0_1), .out2(row0_2), .out3(row0_3), .out4(row0_4), .out5(row0_5), .out6(row0_6),
    .out7(row0_7), .out8(row0_8), .out9(row0_9), .out10(row0_10), .out11(row0_11), .out12(row0_12),
    .out13(row0_13), .out14(row0_14), .out15(row0_15), .out16(row0_16), .out17(row0_17), .out18(row0_18),
    .out19(row0_19), .out20(row0_20), .out21(row0_21), .out22(row0_22), .out23(row0_23), .out24(row0_24),
    .out25(row0_25), .out26(row0_26), .out27(row0_27), .out28(row0_28), .out29(row0_29), .out30(row0_30),
    .out31(row0_31), .in(shifter_4_out), .sel(rowPos));
  Demultiplexer #(.select(5), .width(24), .disabled(0), .enable("false")) demultiplexer_2 (
    .out0(row2_0), .out1(row2_1), .out2(row2_2), .out3(row2_3), .out4(row2_4), .out5(row2_5), .out6(row2_6),
    .out7(row2_7), .out8(row2_8), .out9(row2_9), .out10(row2_10), .out11(row2_11), .out12(row2_12),
    .out13(row2_13), .out14(row2_14), .out15(row2_15), .out16(row2_16), .out17(row2_17), .out18(row2_18),
    .out19(row2_19), .out20(row2_20), .out21(row2_21), .out22(row2_22), .out23(row2_23), .out24(row2_24),
    .out25(row2_25), .out26(row2_26), .out27(row2_27), .out28(row2_28), .out29(row2_29), .out30(row2_30),
    .out31(row2_31), .in(shifter_3_out), .sel(rowPos));
  Counter #(.width(1), .max('h1), .ongoal("load")) counter_2 (
    .D(1'b1), .carry(right_t), .clk(right), .clr(left));  // open: load, count, Q
  Shifter #(.width(24), .shift("rl")) shifter_5 (.in(24'h7), .\dist (colPos1), .out(shifter_5_out));
  Shifter #(.width(24), .shift("rl")) shifter_6 (.in(24'h7), .\dist (colPos1), .out(shifter_6_out));
  Shifter #(.width(24), .shift("rr")) shifter_7 (.in(shifter_5_out), .\dist (colPos2), .out(shifter_7_out));
  Shifter #(.width(24), .shift("rr")) shifter_8 (.in(shifter_6_out), .\dist (colPos2), .out(shifter_8_out));
  Demultiplexer #(.select(5), .width(24), .disabled(0), .enable("false")) demultiplexer_3 (
    .out0(row1_0), .out1(row1_1), .out2(row1_2), .out3(row1_3), .out4(row1_4), .out5(row1_5), .out6(row1_6),
    .out7(row1_7), .out8(row1_8), .out9(row1_9), .out10(row1_10), .out11(row1_11), .out12(row1_12),
    .out13(row1_13), .out14(row1_14), .out15(row1_15), .out16(row1_16), .out17(row1_17), .out18(row1_18),
    .out19(row1_19), .out20(row1_20), .out21(row1_21), .out22(row1_22), .out23(row1_23), .out24(row1_24),
    .out25(row1_25), .out26(row1_26), .out27(row1_27), .out28(row1_28), .out29(row1_29), .out30(row1_30),
    .out31(row1_31), .in(shifter_7_out), .sel(rowPos));
  Demultiplexer #(.select(5), .width(24), .disabled(0), .enable("false")) demultiplexer_4 (
    .out0(row3_0), .out1(row3_1), .out2(row3_2), .out3(row3_3), .out4(row3_4), .out5(row3_5), .out6(row3_6),
    .out7(row3_7), .out8(row3_8), .out9(row3_9), .out10(row3_10), .out11(row3_11), .out12(row3_12),
    .out13(row3_13), .out14(row3_14), .out15(row3_15), .out16(row3_16), .out17(row3_17), .out18(row3_18),
    .out19(row3_19), .out20(row3_20), .out21(row3_21), .out22(row3_22), .out23(row3_23), .out24(row3_24),
    .out25(row3_25), .out26(row3_26), .out27(row3_27), .out28(row3_28), .out29(row3_29), .out30(row3_30),
    .out31(row3_31), .in(shifter_8_out), .sel(rowPos));
  assign out_7 = row3_28 | row2_29 | row1_30 | row0_31;  // OR_Gate or_1, 24 bits wide
  assign out_8 = row3_27 | row2_28 | row1_29 | row0_30;  // OR_Gate or_2, 24 bits wide
  assign out_9 = row3_26 | row2_27 | row1_28 | row0_29;  // OR_Gate or_3, 24 bits wide
  assign out_10 = row3_25 | row2_26 | row1_27 | row0_28;  // OR_Gate or_4, 24 bits wide
  assign out_11 = row3_24 | row2_25 | row1_26 | row0_27;  // OR_Gate or_5, 24 bits wide
  assign out_12 = row3_23 | row2_24 | row1_25 | row0_26;  // OR_Gate or_6, 24 bits wide
  assign out_13 = row3_22 | row2_23 | row1_24 | row0_25;  // OR_Gate or_7, 24 bits wide
  assign out_14 = row3_21 | row2_22 | row1_23 | row0_24;  // OR_Gate or_8, 24 bits wide
  assign out_15 = row3_20 | row2_21 | row1_22 | row0_23;  // OR_Gate or_9, 24 bits wide
  assign out_16 = row3_19 | row2_20 | row1_21 | row0_22;  // OR_Gate or_10, 24 bits wide
  assign out_17 = row3_18 | row2_19 | row1_20 | row0_21;  // OR_Gate or_11, 24 bits wide
  assign out_18 = row3_17 | row2_18 | row1_19 | row0_20;  // OR_Gate or_12, 24 bits wide
  assign out_19 = row3_16 | row2_17 | row1_18 | row0_19;  // OR_Gate or_13, 24 bits wide
  assign out_20 = row3_15 | row2_16 | row1_17 | row0_18;  // OR_Gate or_14, 24 bits wide
  assign out_21 = row3_14 | row2_15 | row1_16 | row0_17;  // OR_Gate or_15, 24 bits wide
  assign out_22 = row3_13 | row2_14 | row1_15 | row0_16;  // OR_Gate or_16, 24 bits wide
  assign out_23 = row3_12 | row2_13 | row1_14 | row0_15;  // OR_Gate or_17, 24 bits wide
  assign out_24 = row3_11 | row2_12 | row1_13 | row0_14;  // OR_Gate or_18, 24 bits wide
  assign out_25 = row3_10 | row2_11 | row1_12 | row0_13;  // OR_Gate or_19, 24 bits wide
  assign out_26 = row3_9 | row2_10 | row1_11 | row0_12;  // OR_Gate or_20, 24 bits wide
  assign out_27 = row3_8 | row2_9 | row1_10 | row0_11;  // OR_Gate or_21, 24 bits wide
  assign out_28 = row3_7 | row2_8 | row1_9 | row0_10;  // OR_Gate or_22, 24 bits wide
  assign out_29 = row3_6 | row2_7 | row1_8 | row0_9;  // OR_Gate or_23, 24 bits wide
  assign out_30 = row3_5 | row2_6 | row1_7 | row0_8;  // OR_Gate or_24, 24 bits wide
  assign out_31 = row3_4 | row2_5 | row1_6 | row0_7;  // OR_Gate or_25, 24 bits wide
  assign out_32 = row3_3 | row2_4 | row1_5 | row0_6;  // OR_Gate or_26, 24 bits wide
  assign out_33 = row3_2 | row2_3 | row1_4 | row0_5;  // OR_Gate or_27, 24 bits wide
  assign out_34 = row3_1 | row2_2 | row1_3 | row0_4;  // OR_Gate or_28, 24 bits wide
  assign out_35 = row3_0 | row2_1 | row1_2 | row0_3;  // OR_Gate or_29, 24 bits wide
  assign out_36 = row3_31 | row2_0 | row1_1 | row0_2;  // OR_Gate or_30, 24 bits wide
  assign out_37 = row3_30 | row2_31 | row1_0 | row0_1;  // OR_Gate or_31, 24 bits wide
  assign out_38 = row3_29 | row2_30 | row1_31 | row0_0;  // OR_Gate or_32, 24 bits wide
endmodule

// intro
module introStart (
  output [23:0] out_1,
  output [23:0] out_2,
  output [23:0] out_3,
  output [23:0] out_4,
  output [23:0] out_5,
  output [23:0] out_6,
  output [23:0] out_7,
  output [23:0] out_8,
  output [23:0] out_9
);


  assign out_1 = 24'hf7bdcf;
  assign out_2 = 24'hc335a6;
  assign out_3 = 24'h333dc6;
  assign out_4 = 24'hf335a6;
  assign out_5 = {24{1'b0}};
  assign out_6 = 24'h3dedbc;
  assign out_7 = 24'h31afb8;
  assign out_8 = 24'h35eab0;
  assign out_9 = 24'h3da8bc;
endmodule
